# Fritzing sketch winston and jousset (saved by Fritzing 0.9.3b)
breadboards: 1

parts:
  HPF_cut = Rotary Potentiometer (Small) [maximum_resistance=100kΩ package=THT]
  LPF_cut = Rotary Potentiometer (Small) [maximum_resistance=100kΩ package=THT]
  220nF = Capacitor [package=cap-pth-small-kit]
  BPF = Toggle Switch [package=THT]
  LPF_IN = 3.5mm Audio Jack [package=audio-jack-3.5mm-smd]
  HPF_IN = 3.5mm Audio Jack [package=audio-jack-3.5mm-smd]
  HPF_OUT = 3.5mm Audio Jack [package=audio-jack-3.5mm-smd]
  LPF_OUT = 3.5mm Audio Jack [package=audio-jack-3.5mm-smd]
  220nF1 = Capacitor [package=cap-pth-small-kit]

nets:
  GND: HPF_cut.wiper, 220nF.2, LPF_IN.SLEEVE, HPF_IN.SLEEVE, HPF_OUT.SLEEVE, LPF_OUT.SLEEVE
  N1: HPF_cut.leg2, HPF_OUT.LEFT, 220nF1.2
  N2: LPF_cut.wiper, 220nF.1
  N3: LPF_cut.leg2, BPF.L1, LPF_IN.LEFT, LPF_OUT.LEFT
  N4: BPF.COM, HPF_IN.LEFT, 220nF1.1
