# Fritzing sketch VCO CEM3340 (saved by Fritzing 0.9.3b)
breadboards: 1

parts:
  R1 = Resistor [tolerance=±5% resistance=10k package=THT]
  R2 = Resistor [tolerance=±5% resistance=10k package=THT]
  R3 = Resistor [tolerance=±5% resistance=100k package=THT]
  R4 = Resistor [tolerance=±5% resistance=100k package=THT]
  R5 = Resistor [tolerance=±5% resistance=100k package=THT]
  TL072 = Dual Op-Amp [package=dip08]
  TL072_2 = Dual Op-Amp [package=dip08]
  IC3 = CEM3340
  R6 = TRIMPOT [package=3386u]
  Tune = POT [package=pot_mammoth]
  PWM = POT [package=pot_mammoth]
  PWM_CV = POT [package=pot_mammoth]
  CV_PWM = 3.5mm Audio Jack [package=audio-jack-3.5mm-smd]
  square = 3.5mm Audio Jack [package=audio-jack-3.5mm-smd]
  CV_in = 3.5mm Audio Jack [package=audio-jack-3.5mm-smd]
  R7 = Resistor [tolerance=±5% resistance=22k package="1206 [SMD]"]
  R8 = Resistor [tolerance=±5% resistance=4.7k package="1206 [SMD]"]
  FM = POT [package=pot_mammoth]
  FM_2 = 3.5mm Audio Jack [package=audio-jack-3.5mm-smd]
  R9 = Resistor [tolerance=±5% resistance=680 package="1206 [SMD]"]
  C2 = Ceramic Capacitor [capacitance=0.1nF package="0805 [SMD, multilayer]"]
  C4 = Ceramic Capacitor [capacitance=10nF package="1206 [SMD, multilayer]"]
  R10 = Resistor [tolerance=±5% resistance=470 package="1206 [SMD]"]
  R11 = Resistor [tolerance=±5% resistance=1M package="1206 [SMD]"]
  R12 = Resistor [tolerance=±5% resistance=470k package="1206 [SMD]"]
  R13 = Resistor [tolerance=±5% resistance=2.2k package="1206 [SMD]"]
  R14 = Resistor [tolerance=±5% resistance=470k package="1206 [SMD]"]
  R15 = Resistor [tolerance=±5% resistance=100k package=THT]
  triangle = 3.5mm Audio Jack [package=audio-jack-3.5mm-smd]
  saw = 3.5mm Audio Jack [package=audio-jack-3.5mm-smd]
  R16 = Resistor [tolerance=±5% resistance=470k package="1206 [SMD]"]
  R17 = Resistor [tolerance=±5% resistance=1M package=THT]
  C5 = Ceramic Capacitor [capacitance="100 nF" package="0603 [SMD, multilayer]"]

nets:
  GND: R1.Pin_0, R2.Pin_0, PWM.E, PWM_CV.E, CV_PWM.SLEEVE, square.SLEEVE, CV_in.SLEEVE, FM.E, FM_2.SLEEVE, triangle.SLEEVE, saw.SLEEVE
  N1: R1.Pin_1, IC3.pin_4
  N2: R2.Pin_1, TL072.A_+IN
  N3: R3.Pin_0, CV_in.LEFT
  N4: R3.Pin_1, R5.Pin_1, IC3.pin15, R14.Pin_0
  N5: R4.Pin_0, TL072_2.B_+IN, R15.Pin_0
  N6: R4.Pin_1, PWM_CV.S
  N7: R5.Pin_0, Tune.S
  N8: TL072.A_OUT, TL072.A_-IN, square.LEFT
  -12V: TL072.A_V-, TL072_2.A_V-, R9.Pin_0
  N9: TL072.B_+IN, IC3.pin10
  N10: TL072.B_-IN, TL072.B_OUT, triangle.LEFT
  12V: TL072.A_V+, TL072_2.A_V+, IC3.pin16, Tune.A, PWM.A, R12.Pin_0
  N11: TL072_2.A_OUT, TL072_2.A_-IN, saw.LEFT
  N12: TL072_2.A_+IN, IC3.pin8
  N13: TL072_2.B_-IN, TL072_2.B_OUT, R16.Pin_1
  N14: IC3.pin1, R7.Pin_1
  N15: IC3.pin2, R8.Pin_1
  N16: IC3.pin3, R6.WIPER, R6.CW, R8.Pin_0, R9.Pin_1
  N17: IC3.pin5, R16.Pin_0
  N18: IC3.pin11, C2.0
  N19: IC3.pin12, C2.1, R10.Pin_1
  N20: IC3.pin13, R10.Pin_0, R11.Pin_0, R17.Pin_0
  N21: IC3.pin14, R13.Pin_0
  N22: R6.CCW, R7.Pin_0
  N23: PWM.S, R15.Pin_1
  N24: PWM_CV.A, CV_PWM.LEFT
  N25: FM.S, FM_2.LEFT
  N26: FM.A, C5.1
  N27: C4.0, R14.Pin_1
  N28: C4.1, R13.Pin_1
  N29: R11.Pin_1, R12.Pin_1
  N30: R17.Pin_1, C5.0
