# Fritzing sketch 555 LFO (saved by Fritzing 0.9.3b)
breadboards: 1

parts:
  U1 = 555 Timer [package="DIP8 [THT]"]
  C1 = Electrolytic Capacitor [capacitance=10µF package="100 mil [THT, electrolytic]"]
  R1 = Rotary Potentiometer (Small) [maximum_resistance=10kΩ package=THT]
  R2 = Resistor [tolerance=±5% resistance=1k package=THT]
  LED1 = LED - 5mm [color="Red (633nm)" package="5 mm [THT]"]
  out = Audio Jack (TRS) 3.5mm [package="4Ucon 08780 [THT]"]
  R3 = Photocell (LDR) [package=THT]
  R4 = Photocell (LDR) [package=THT]
  C2 = Ceramic Capacitor [capacitance=220nF voltage=16V package="100 mil [THT, multilayer]"]
  in = Audio Jack (TRS) 3.5mm [package="4Ucon 08780 [THT]"]
  tremolo_out = Audio Jack (TRS) 3.5mm [package="4Ucon 08780 [THT]"]
  filter_out = Audio Jack (TRS) 3.5mm [package="4Ucon 08780 [THT]"]

nets:
  GND: U1.Ground, C1.-, LED1.cathode, out.Sleeve, C2.1, in.Sleeve, tremolo_out.Sleeve, filter_out.Sleeve
  N1: U1.Trigger, U1.Threshold, C1.+, R1.wiper
  N2: U1.Output, LED1.anode, out.Ring, out.Tip
  9V: U1.Reset, U1.Vcc_Supply_Voltage, R2.Pin_0
  N3: U1.Discharge, R1.leg2, R2.Pin_1
  N4: R3.pin_0, C2.0
  N5: R3.pin_1, filter_out.Ring
  N6: R4.pin_0, tremolo_out.Ring, tremolo_out.Tip
  N7: R4.pin_1, in.Ring, in.Tip, filter_out.Tip
