# Fritzing sketch crossfader (saved by Fritzing 0.9.3b)
breadboards: 1

parts:
  R1 = Rotary Potentiometer (Small) [maximum_resistance=10kΩ package=THT]
  A = Audio Jack (TRS) 3.5mm [package="4Ucon 08780 [THT]"]
  Y = Audio Jack (TRS) 3.5mm [package="4Ucon 08780 [THT]"]
  B = Audio Jack (TRS) 3.5mm [package="4Ucon 08780 [THT]"]

nets:
  N1: R1.leg1, B.Tip
  N2: R1.wiper, A.Tip
  N3: R1.leg2, Y.Tip
  GND: A.Sleeve, Y.Sleeve, B.Sleeve
