# Fritzing sketch distortion (saved by Fritzing 0.9.3b)
breadboards: 1

parts:
  R1 = Resistor [tolerance=±5% resistance=100k package=THT]
  3904 = NPN-Transistor [package="TO92 [THT]"]
  1N4148 = Diode [package=diode-1n4001]
  1N4148- = Diode [package=diode-1n4001]
  100_μF = Capacitor Polarized [package=nippon_f80]
  10_μF = Capacitor Polarized [package=nippon_f80]
  R2 = Resistor [tolerance=±5% resistance=10k package=THT]
  R3 = Resistor [tolerance=±5% resistance=100k package=THT]
  OUT = 2.5mm Audio Jack [package=stereojack2.5mm_specia_pogopins]
  IN = 2.5mm Audio Jack [package=stereojack2.5mm_specia_pogopins]

nets:
  GND: R1.Pin_0, 3904.E, 1N4148.A, 1N4148-.C, OUT.SLEEVE, IN.SLEEVE
  N1: R1.Pin_1, 1N4148.C, 1N4148-.A, 10_μF.-, OUT.LEFT
  N2: 3904.B, 100_μF.+, R2.Pin_1, R3.Pin_0
  N3: 3904.C, 10_μF.+, R3.Pin_1
  N4: 100_μF.-, IN.LEFT
  9V: R2.Pin_0
