# Fritzing sketch mono to stereo (saved by Fritzing 0.9.3b)
breadboards: 1

parts:
  Left = 2.5mm Audio Jack [package=stereojack2.5mm_stereojack2.5mm]
  Right = 2.5mm Audio Jack [package=stereojack2.5mm_stereojack2.5mm]
  Stereo = 2.5mm Audio Jack [package=stereojack2.5mm_stereojack2.5mm]

nets:
  GND: Left.SLEEVE, Right.SLEEVE, Stereo.SLEEVE
  N1: Left.LEFT, Stereo.LEFT
  N2: Right.LEFT, Stereo.RIGHT
