# Fritzing sketch arduino synth (saved by Fritzing 0.9.3b)
breadboards: 1

parts:
  Composant1 = Arduino Uno (Rev3) - ICSP
  midi_in = DIN-5 jack (MIDI) [package=THT]
  out = 3.5mm Audio Jack [package=audio-jack-3.5mm-smd]

nets:
  N1: Composant1.D9_PWM, out.LEFT
  GND: Composant1.GND, midi_in.2, midi_in.GND, out.SLEEVE
  N2: Composant1.D0/RX, midi_in.5
