# Fritzing sketch Pages Filter (1) (saved by Fritzing 0.8.7b)
breadboards: 1

parts:
  R1 = Resistor [tolerance=±5% resistance=220 package=THT]
  C1 = Ceramic Capacitor [capacitance=100nF package="100 mil [THT, multilayer]"]
  R2 = Rotary Potentiometer (Small) [maximum_resistance=100kΩ package=THT]
  R3 = Resistor [tolerance=±5% resistance=220 package=THT]
  OUT = female pin header, 2 pins [form="♀ (female)"]
  IN = female pin header, 2 pins [form="♀ (female)"]
  S1 = Toggle Switch [package=THT]

nets:
  N1: R1.Pin_0, IN.pin2, S1.L2
  N2: R1.Pin_1, R2.leg2, R3.Pin_0
  N3: C1.0, IN.pin1, S1.L1
  N4: C1.1, R2.wiper, R3.Pin_1, OUT.pin2
  N5: OUT.pin1, S1.COM
