# Fritzing sketch Turing machine (saved by Fritzing 0.9.3b)
breadboards: 1

parts:
  Composant1 = Arduino Nano (Rev3.0)
  SUB = Rotary Potentiometer (Small) [maximum_resistance=100kΩ package=THT]
  MCP4921 = IC, DIP package, 8 pins [chip_label=IC]
  MAIN = Rotary Potentiometer (Small) [maximum_resistance=100kΩ package=THT]
  D1 = Schottky Diode [part_number=BAT43 package="Melf DO-213 AB [SMD]"]
  R1 = Resistor [tolerance=±5% resistance=470 package=THT]
  D2 = Schottky Diode [part_number=BAT43 package="Melf DO-213 AB [SMD]"]
  R2 = Resistor [tolerance=±5% resistance=22k package=THT]
  LED1 = LED - 5mm [color="Red (633nm)" package="5 mm [THT]"]
  Gate_Out = Audio Jack (TRS) 3.5mm [package="4Ucon 08780 [THT]"]
  R3 = Resistor [tolerance=±5% resistance=10k package=THT]
  LED2 = LED - 5mm [color="Red (633nm)" package="5 mm [THT]"]
  S1 = SPST Switch [package=switch-spdt_kit]
  clock_in = Audio Jack (TRS) 3.5mm [package="4Ucon 08780 [THT]"]
  D3 = Schottky Diode [part_number=BAT43 package="Melf DO-213 AB [SMD]"]
  D4 = Schottky Diode [part_number=BAT43 package="Melf DO-213 AB [SMD]"]
  R5 = Resistor [tolerance=±5% resistance=470 package=THT]
  Out = Audio Jack (TRS) 3.5mm [package="4Ucon 08780 [THT]"]
  R6 = Resistor [tolerance=±5% resistance=470 package=THT]
  D5 = Schottky Diode [part_number=BAT43 package="Melf DO-213 AB [SMD]"]
  D6 = Schottky Diode [part_number=BAT43 package="Melf DO-213 AB [SMD]"]
  R7 = Resistor [tolerance=±5% resistance=100k package="0805 [SMD]"]
  R4 = Resistor [tolerance=±5% resistance=470 package=THT]
  R8 = Resistor [tolerance=±5% resistance=470 package=THT]
  220pF = Capacitor [package=cap-pth-small2]
  220pF1 = Capacitor [package=cap-pth-small2]

nets:
  GND: Composant1.GND, SUB.leg1, MCP4921.pin7, MAIN.leg1, D1.anode, D2.cathode, LED1.cathode, Gate_Out.Sleeve, LED2.cathode, S1.P, clock_in.Sleeve, D4.anode, Out.Sleeve, D6.anode, R7.Pin_1, 220pF.2, 220pF1.2
  N1: Composant1.D2, S1.O
  N2: Composant1.D4, S1.S
  N3: Composant1.D5, D1.cathode, R1.Pin_0, D2.anode, R2.Pin_0
  N4: Composant1.D6, R3.Pin_0
  N5: Composant1.D7, R6.Pin_1, D5.anode, D6.cathode, R7.Pin_0
  N6: Composant1.D9, MCP4921.pin5
  N7: Composant1.D11/MOSI, MCP4921.pin4
  12V: Composant1.VIN
  N8: Composant1.5V, SUB.leg2, MCP4921.pin1, MCP4921.pin6, MAIN.leg2, D5.cathode
  N9: Composant1.A4, R8.Pin_1, 220pF.1
  N10: Composant1.A2, R4.Pin_1, 220pF1.1
  N11: Composant1.D13/SCK, MCP4921.pin3
  N12: SUB.wiper, R8.Pin_0
  N13: MCP4921.pin8, D3.anode, D4.cathode, R5.Pin_0
  N14: MAIN.wiper, R4.Pin_0
  N15: R1.Pin_1, Gate_Out.Tip
  N16: R2.Pin_1, LED1.anode
  N17: R3.Pin_1, LED2.anode
  N18: clock_in.Tip, R6.Pin_0
  5V: D3.cathode
  N19: R5.Pin_1, Out.Tip
