# Fritzing sketch white noise (saved by Fritzing 0.9.3b)
breadboards: 1

parts:
  2n3904 = NPN-Transistor [package="TO92 [THT]"]
  2n3904_2 = NPN-Transistor [package="TO92 [THT]"]
  C1 = Ceramic Capacitor [capacitance=004.7µF package="100 mil [THT, multilayer]"]
  C2 = Ceramic Capacitor [capacitance=004.7µF package="100 mil [THT, multilayer]"]
  R1 = Resistor [tolerance=±5% resistance=470k package=THT]
  R2 = Resistor [tolerance=±5% resistance=4.7k package=THT]
  U1 = 3.5mm Audio Jack [package=audio-jack-3.5mm-smd]
  R3 = Resistor [tolerance=±5% resistance=470k package=THT]

nets:
  12V: 2n3904.E, R2.Pin_0
  N1: 2n3904.B, C1.1, R1.Pin_0, R3.Pin_1
  GND: 2n3904_2.E, U1.SLEEVE, R3.Pin_0
  N2: 2n3904_2.B, C1.0
  N3: 2n3904_2.C, C2.0, R1.Pin_1, R2.Pin_1
  N4: C2.1, U1.LEFT
