# Fritzing sketch octave up (saved by Fritzing 0.9.3b)
breadboards: 1

parts:
  Q1 = NPN-Transistor [package="TO92 [THT]"]
  Q2 = NPN-Transistor [package="TO92 [THT]"]
  Q3 = PNP-Transistor [package="TO92 [THT]"]
  C1 = Electrolytic Capacitor [capacitance=10µF package="100 mil [THT, electrolytic]"]
  C2 = Electrolytic Capacitor [capacitance=10µF package="100 mil [THT, electrolytic]"]
  C3 = Ceramic Capacitor [capacitance=100nF package="100 mil [THT, multilayer]"]
  R1 = Resistor [tolerance=±5% resistance=470 package=THT]
  R2 = Resistor [tolerance=±5% resistance=470 package=THT]
  C4 = Ceramic Capacitor [capacitance=100nF package="100 mil [THT, multilayer]"]
  C5 = Ceramic Capacitor [capacitance=100nF package="100 mil [THT, multilayer]"]
  R3 = Resistor [tolerance=±5% resistance=1M package=THT]
  R4 = Resistor [tolerance=±5% resistance=470k package=THT]
  OUT = Audio Jack (TRS) 3.5mm [package="PG203J [THT]"]
  IN = Audio Jack (TRS) 3.5mm [package="PG203J [THT]"]
  R5 = Resistor [tolerance=±5% resistance=10k package=THT]
  C6 = Ceramic Capacitor [capacitance=100nF package="100 mil [THT, multilayer]"]
  VOLUME = Rotary Potentiometer (Large) [maximum_resistance=100kΩ package=THT]
  R6 = Resistor [tolerance=±5% resistance=10k package=THT]
  R7 = Resistor [tolerance=±5% resistance=10k package=THT]
  R8 = Resistor [tolerance=±5% resistance=470 package="0805 [SMD]"]

nets:
  N1: Q1.E, R1.Pin_0
  N2: Q1.B, C3.1, R3.Pin_0
  N3: Q1.C, C4.0, R3.Pin_1, R6.Pin_0, R7.Pin_1, R8.Pin_1
  N4: Q2.E, Q3.C, R4.Pin_1, R5.Pin_0, C6.1
  N5: Q2.B, C4.1
  N6: Q2.C, Q3.E, R6.Pin_1
  N7: Q3.B, C5.1
  GND: C1.-, C2.-, R2.Pin_1, OUT.Sleeve, IN.Sleeve, R5.Pin_1, VOLUME.leg1
  N8: C1.+, R1.Pin_1, R2.Pin_0
  N9: C2.+, R7.Pin_0
  N10: C3.0, IN.Tip
  N11: C5.0, R4.Pin_0
  N12: OUT.Tip, VOLUME.wiper
  N13: C6.0, VOLUME.leg2
  9V: R8.Pin_0
