# Fritzing sketch preampli (saved by Fritzing 0.9.3b)
breadboards: 1

parts:
  R1 = Resistor [tolerance=±5% resistance=4.7k package=THT]
  R2 = Resistor [tolerance=±5% resistance=150k package=THT]
  C1 = Ceramic Capacitor [capacitance=100nF package="100 mil [THT, multilayer]"]
  R3 = Resistor [tolerance=±5% resistance=100k package=THT]
  C2 = Electrolytic Capacitor [capacitance=4.7µF package="100 mil [THT, electrolytic]"]
  volume = Rotary Potentiometer (Small) [maximum_resistance=100kΩ package=THT]
  Gain = Rotary Potentiometer (Small) [maximum_resistance=100kΩ package=THT]
  in = Audio Jack (TRS) 3.5mm [package="4Ucon 08780 [THT]"]
  R6 = Resistor [tolerance=±5% resistance=47k package=THT]
  out = Audio Jack (TRS) 3.5mm [package="4Ucon 08780 [THT]"]
  MCP6002 = IC, DIP package, 8 pins [chip_label=IC]

nets:
  N1: R1.Pin_0, C2.+
  N2: R1.Pin_1, R2.Pin_0, MCP6002.pin6
  N3: R2.Pin_1, volume.leg1, MCP6002.pin7
  N4: C1.0, Gain.wiper
  N5: C1.1, R3.Pin_0, R6.Pin_1, MCP6002.pin5
  5V: R3.Pin_1, MCP6002.pin4
  GND: C2.-, volume.leg2, Gain.leg2, in.Sleeve, R6.Pin_0, out.Sleeve, MCP6002.pin8
  N6: volume.wiper, out.Tip
  N7: Gain.leg1, in.Tip
