# Fritzing sketch random midi generator (saved by Fritzing 0.9.3b)
breadboards: 1

parts:
  DIN1 = DIN-5 jack (MIDI) [package=THT]
  Composant1 = Arduino Uno (Rev3) - ICSP
  R1 = Rotary Potentiometer (Small) [maximum_resistance=100kΩ package=THT]
  R2 = Resistor [tolerance=±5% resistance=220 package=THT]
  R3 = Resistor [tolerance=±5% resistance=220 package=THT]
  S1 = Toggle Switch [package=THT]
  S2 = Toggle Switch [package=THT]
  R4 = Resistor [tolerance=±5% resistance=100k package=THT]

nets:
  N1: DIN1.5, R2.Pin_0
  GND: DIN1.2, DIN1.GND, Composant1.GND
  N2: DIN1.4, R3.Pin_0
  N3: Composant1.5V, R1.leg2, R3.Pin_1, R4.Pin_0
  N4: Composant1.D10_PWM/SS, S2.L2
  N5: Composant1.D11_PWM/MOSI, S1.L2
  N6: Composant1.A5/SCL, R1.wiper
  N7: Composant1.D1/TX, R2.Pin_1
  N8: S1.COM, S2.COM, R4.Pin_1
