# Fritzing sketch roland system 100 LFO (saved by Fritzing 0.9.3b)
breadboards: 1

parts:
  R1 = Resistor [tolerance=±5% resistance=10k package=THT]
  C1 = Ceramic Capacitor [capacitance=100nF package="100 mil [THT, multilayer]"]
  Rate = Rotary Potentiometer (Small) [maximum_resistance=100kΩ package=THT]
  R3 = Resistor [tolerance=±5% resistance=10k package=THT]
  LED1 = smd LED [color="Red (633nm)" package="0805 [SMD]"]
  R4 = Resistor [tolerance=±5% resistance=15k package=THT]
  R5 = Resistor [tolerance=±5% resistance=2.2k package=THT]
  C2 = Ceramic Capacitor [capacitance=100nF package="100 mil [THT, multilayer]"]
  C3 = Ceramic Capacitor [capacitance=10nF package="100 mil [THT, multilayer]"]
  Range = SPST Switch [package=switch-spdt_lock.007s]
  IC1 = Dual Op-Amp [package=dip08]
  R6 = Resistor [tolerance=±5% resistance=4.7k package=THT]
  R7 = Resistor [tolerance=±5% resistance=1M package=THT]
  Triangle = Audio Jack (TRS) 3.5mm [package="4Ucon 08780 [THT]"]
  square = Audio Jack (TRS) 3.5mm [package="4Ucon 08780 [THT]"]

nets:
  N1: R1.Pin_0, Rate.leg2
  N2: R1.Pin_1, IC1.A_OUT, R6.Pin_0, square.Tip
  N3: C1.0, C2.0, Range.O
  N4: C1.1, C2.1, C3.1, IC1.B_-IN, R7.Pin_1
  N5: Rate.leg1, R4.Pin_0
  N6: Rate.wiper, R5.Pin_0, R7.Pin_0
  N7: R3.Pin_0, R4.Pin_1, IC1.A_+IN
  N8: R3.Pin_1, Range.P, IC1.B_OUT, Triangle.Tip
  N9: LED1.cathode, R6.Pin_1
  N10: LED1.anode, IC1.A_-IN
  GND: R5.Pin_1, Triangle.Sleeve, square.Sleeve
  N11: C3.0, Range.S
  -12V: IC1.A_V-
  12V: IC1.A_V+
