# Fritzing sketch sample and hold (saved by Fritzing 0.9.3b)
breadboards: 1

parts:
  J113 = TRANSISTOR_NPN_2 [package=to-92]
  R1 = Resistor [tolerance=±5% resistance=1M package=THT]
  R2 = Rotary Potentiometer (Small) [maximum_resistance=100kΩ package=THT]
  C1 = Ceramic Capacitor [capacitance=100nF package="100 mil [THT, multilayer]"]
  D1 = Rectifier Diode [part_number=1N4148 package="300 mil [THT]"]
  C2 = Ceramic Capacitor [capacitance=1nF package="100 mil [THT, multilayer]"]
  R3 = Resistor [tolerance=±5% resistance=33k package=THT]
  D2 = Rectifier Diode [part_number=1N4148 package="300 mil [THT]"]
  out = Audio Jack (TRS) 3.5mm [package="4Ucon 08780 [THT]"]
  Clock_in = Audio Jack (TRS) 3.5mm [package="4Ucon 08780 [THT]"]
  Signal = Audio Jack (TRS) 3.5mm [package="4Ucon 08780 [THT]"]
  R8 = Resistor [tolerance=±5% resistance=100k package=THT]
  R9 = Resistor [tolerance=±5% resistance=100k package=THT]
  R10 = Resistor [tolerance=±5% resistance=1k package=THT]
  TL074 = IC, DIP package, 14 pins [chip_label=IC]
  R11 = Resistor [tolerance=±5% resistance=100k package=THT]

nets:
  N1: J113.C, R1.Pin_1
  N2: J113.B, R1.Pin_0, D1.anode, TL074.pin6, TL074.pin7
  N3: J113.E, C1.1, TL074.pin12
  GND: R2.leg1, C1.0, R3.Pin_0, out.Sleeve, Clock_in.Sleeve, Signal.Sleeve, R8.Pin_1, R9.Pin_1
  N4: R2.wiper, TL074.pin5
  N5: R2.leg2, Signal.Ring, Signal.Tip
  N6: D1.cathode, TL074.pin1
  N7: C2.0, Clock_in.Ring, Clock_in.Tip
  N8: C2.1, D2.anode, R9.Pin_0
  N9: R3.Pin_1, TL074.pin2, R11.Pin_0
  N10: D2.cathode, R8.Pin_0, TL074.pin3
  N11: out.Ring, out.Tip, R10.Pin_1
  N12: R10.Pin_0, TL074.pin13, TL074.pin14
