# Fritzing sketch wavefolder (saved by Fritzing 0.9.3b)
breadboards: 1

parts:
  R1 = Resistor [tolerance=±5% resistance=10k package=THT]
  2N3906 = PNP-Transistor [package="TO92 [THT]"]
  2N3904 = TRANSISTOR_NPN [package=to-92-ammo]
  R2 = Resistor [tolerance=±5% resistance=1k package="2512 [SMD]"]
  R3 = Resistor [tolerance=±5% resistance=2.2k package="2512 [SMD]"]
  R4 = Rotary Potentiometer (Small) [maximum_resistance=100kΩ package=THT]
  TL072 = Dual Op-Amp [package=dip08]
  in = 3.5mm Audio Jack [package=audio-jack-3.5mm-smd]
  Triangle = 3.5mm Audio Jack [package=audio-jack-3.5mm-smd]
  square = 3.5mm Audio Jack [package=audio-jack-3.5mm-smd]
  R5 = Resistor [tolerance=±5% resistance=1k package="2512 [SMD]"]
  R6 = Resistor [tolerance=±5% resistance=15k package="2512 [SMD]"]
  R7 = Resistor [tolerance=±5% resistance=15k package="2512 [SMD]"]

nets:
  N1: R1.Pin_0, 2N3906.C, 2N3904.C, TL072.B_-IN
  N2: R1.Pin_1, TL072.A_-IN
  N3: 2N3906.E, R6.Pin_0
  N4: 2N3906.B, 2N3904.B, R4.wiper
  N5: 2N3904.E, R7.Pin_0
  N6: R2.Pin_0, TL072.A_OUT
  N7: R2.Pin_1, Triangle.RIGHT, Triangle.LEFT
  N8: R3.Pin_0, TL072.B_OUT
  N9: R3.Pin_1, square.RIGHT, square.LEFT, R5.Pin_0
  GND: R4.leg1, TL072.A_+IN, TL072.B_+IN, in.SLEEVE, Triangle.SLEEVE, square.SLEEVE, R5.Pin_1
  N10: R4.leg2, in.RIGHT, in.LEFT
  -12V: TL072.A_V-
  12V: TL072.A_V+, R6.Pin_1, R7.Pin_1
