# Fritzing sketch atari punk (saved by Fritzing 0.9.3b)
breadboards: 1

parts:
  U1 = 555 Timer [package="DIP8 [THT]"]
  U2 = 555 Timer [package="DIP8 [THT]"]
  C1 = Electrolytic Capacitor [capacitance=10µF package="100 mil [THT, electrolytic]"]
  C2 = Ceramic Capacitor [capacitance=100nF package="100 mil [THT, multilayer]"]
  C3 = Ceramic Capacitor [capacitance=10nF package="100 mil [THT, multilayer]"]
  R1 = Resistor [tolerance=±5% resistance=1k package=THT]
  out = Audio Jack (TRS) 3.5mm [package="4Ucon 08780 [THT]"]
  R2 = Rotary Potentiometer (Small) [maximum_resistance=0.5MΩ package=THT]
  R3 = Rotary Potentiometer (Small) [maximum_resistance=0.5MΩ package=THT]

nets:
  GND: U1.Ground, U2.Ground, C2.0, C3.0, out.Sleeve, R2.leg1, R3.leg1
  N1: U1.Trigger, U1.Threshold, C3.1, R1.Pin_0
  N2: U1.Output, U2.Trigger
  5V: U1.Reset, U1.Vcc_Supply_Voltage, U2.Reset, U2.Vcc_Supply_Voltage, R2.leg2, R3.leg2
  N3: U1.Discharge, R1.Pin_1, R2.wiper
  N4: U2.Output, C1.+
  N5: U2.Threshold, U2.Discharge, C2.1, R3.wiper
  N6: C1.-, out.Ring, out.Tip
