# Fritzing sketch filter controller 2600 (saved by Fritzing 0.9.3b)
breadboards: 1

parts:
  R1 = Rotary Potentiometer (Small) [maximum_resistance=100kΩ package=THT]
  103 = Ceramic Capacitor [capacitance=10nF package="100 mil [THT, multilayer]"]
  R2 = Resistor [tolerance=±5% resistance=100k package=THT]
  R3 = Resistor [tolerance=±5% resistance=47k package=THT]
  104 = Ceramic Capacitor [capacitance=100nF package="100 mil [THT, multilayer]"]
  472 = Ceramic Capacitor [capacitance=4.7nF package="100 mil [THT, multilayer]"]
  TRS1 = Audio Jack (TRS) 3.5mm [package="4Ucon 08780 [THT]"]
  out = Audio Jack (TRS) 3.5mm [package="4Ucon 08780 [THT]"]

nets:
  N1: R1.leg1, 104.1
  N2: R1.wiper, R2.Pin_0, 472.1
  N3: R1.leg2, 103.0, R3.Pin_0
  GND: 103.1, R2.Pin_1, TRS1.Sleeve, out.Sleeve
  N4: R3.Pin_1, 472.0, TRS1.Ring, TRS1.Tip
  N5: 104.0, out.Ring, out.Tip
